# Fritzing sketch fauxmo-esp-maplin-socket (saved by Fritzing 0.9.3b)
breadboards: 1

parts:
  U1 = NodeMCU V1.0
  U2 = FS1000A - 433Mhz RF Transmitter [package=THT]

nets:
  N1: U1.D1, U2.DATA
  GND: U1.GND, U2.GND
  VIN: U1.Vin, U2.VCC

custom parts:
  NodeMCU V1.0: ESP8266 based NodeMCU
  FS1000A - 433Mhz RF Transmitter: This is 433Mhz RF transmitter with receiver kit for Arduino ARM MCU wireless Application environment: Remote control switch, receiver module, motorcycles, automobile anti-theft products, home security products, electric doors, shutter doors, windows, remote control socket, remote control LED, remote audio remote control electric doors, garage door remote control, remote control retractable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
